# Fritzing sketch scheme (saved by Fritzing 0.9.3b)
breadboards: 1

parts:
  Raspberry_Pi1 = Raspberry Pi 2  # not connected
  Part1 = Arduino Uno (Rev3)
  5V_Power_Supply = 4 x AAA Battery Mount
  Finger_Servo_2 = Basic Servo
  Finger_Servo_3 = Basic Servo
  Finger_Servo_1 = Basic Servo
  Thumb_Servo = Basic Servo
  Pressure_Sensor_1 = Basic Force Sensing Resistor (FSR) [package=THT]
  Pressure_Sensor_2 = Basic Force Sensing Resistor (FSR) [package=THT]
  Pressure_Sensor_3 = Basic Force Sensing Resistor (FSR) [package=THT]
  Pressure_Sensor_4 = Basic Force Sensing Resistor (FSR) [package=THT]
  Q1 = PHOTOTRANSISTOR REFLECTIVE OBJECT SENSOR [package=qrb1114-side]
  R1 = Resistor [tolerance=±5% resistance=10k package="0805 [SMD]"]
  R2 = Resistor [tolerance=±5% resistance=200 package="0805 [SMD]"]
  Linear_Actuator = Dagu DGServo 9g header connector (female) [package=THT]

nets:
  N1: Part1.A0, Q1.C, R1.Pin_1
  GND: Part1.A1, Part1.A2, Part1.A3, Part1.A4/SDA, Finger_Servo_2.gnd, Finger_Servo_3.gnd, Finger_Servo_1.gnd, Thumb_Servo.gnd, Pressure_Sensor_1.pin_1, Pressure_Sensor_2.pin_1, Pressure_Sensor_3.pin_1, Pressure_Sensor_4.pin_1, Q1.E, Q1.K, Linear_Actuator.gnd
  N2: Part1.D9_PWM, Thumb_Servo.pulse
  N3: Part1.D10_PWM/SS, Linear_Actuator.pulse
  N4: Part1.D3_PWM, Finger_Servo_1.pulse
  N5: Part1.D5_PWM, Finger_Servo_2.pulse
  N6: Part1.D6_PWM, Finger_Servo_3.pulse
  5V: Part1.5V, Finger_Servo_2.vcc, Finger_Servo_3.vcc, Finger_Servo_1.vcc, Thumb_Servo.vcc, Pressure_Sensor_1.pin_0, Pressure_Sensor_2.pin_0, Pressure_Sensor_3.pin_0, Pressure_Sensor_4.pin_0, R1.Pin_0, R2.Pin_0, Linear_Actuator.Vcc
  Micro USB: 5V_Power_Supply.-, 5V_Power_Supply.+
  N7: Q1.A, R2.Pin_1
